# Fritzing sketch Module (saved by Fritzing 1.0.1rc)
breadboards: 1

parts:
  IC1 = IC, DIP package, 6 pins [chip_label=BMP280]
  Part5 = Arduino Pro Mini (3.3V)
  OLED2 = 128x32 I2C Monochrome OLED Display

nets:
  3.3V: IC1.pin1, Part5.VCC, OLED2.3.3V
  GND: IC1.pin2, Part5.GND, OLED2.GND
  SCL: IC1.pin3, Part5.A5, OLED2.SCL
  SDA: IC1.pin4, Part5.A4, OLED2.SDA
