# Fritzing sketch LogicProbe (saved by Fritzing 0.9.2b)
breadboards: 1

parts:
  D1 = LED - 3mm [color="Red (633nm)" package="3 mm [THT]"]
  D3 = LED - 3mm [color="Yellow (595nm)" package="3 mm [THT]"]
  R3 = Resistor [tolerance=±5% resistance=1k package=THT]
  R1 = Resistor [tolerance=±5% resistance=1k package=THT]
  5V = Power plug
  D2 = LED - 3mm [color="Green (555nm)" package="3 mm [THT]"]
  R2 = Resistor [tolerance=±5% resistance=1k package=THT]
  R4 = Resistor [tolerance=±5% resistance=1M package=THT]
  C1 = Ceramic Capacitor [capacitance=100nF package="100 mil [THT, multilayer]"]
  IC1 = IC, DIP package, 14 pins [chip_label=CD4069BE]

nets:
  N1: D1.cathode, D2.anode, IC1.pin2, IC1.pin13
  N2: D1.anode, R1.Pin_1
  N3: D3.cathode, IC1.pin8
  N4: D3.anode, R3.Pin_0
  Vcc: R3.Pin_1, R1.Pin_0, 5V.VCC, R4.Pin_0, IC1.pin14
  GND: 5V.GND, R2.Pin_0, IC1.pin7
  N5: D2.cathode, R2.Pin_1
  N6: R4.Pin_1, C1.1, IC1.pin11
  N7: C1.0, IC1.pin12
  INPUT: IC1.pin1
  N8: IC1.pin9, IC1.pin10

notes:
  INPUT
