# Fritzing sketch LDRComparator (saved by Fritzing 0.9.0b)
breadboards: 1

parts:
  R1 = Photocell (LDR) [package=THT]
  Part1 = Arduino Uno (Rev3)
  R2 = Rotary Potentiometer (Small) [maximum_resistance=50kΩ package=THT]
  R3 = Resistor [tolerance=±5% resistance=4.7k package=THT]
  R4 = Resistor [tolerance=±5% resistance=4.7k package=THT]
  LED1 = LED - 5mm [color="Red (633nm)" package="5 mm [THT]"]
  R5 = Resistor [tolerance=±5% resistance=4.7k package=THT]
  U1 = LMV324 [part_number=LM324 package=so014]

nets:
  N1: R1.pin_0, Part1.5V, R2.leg2, U1.G$1_+V
  N2: R1.pin_1, Part1.A0, R4.Pin_0, U1.G$1_-IN
  N3: Part1.D7, LED1.anode, U1.G$1_OUT
  N4: Part1.GND, R3.Pin_1, R4.Pin_1, R5.Pin_1, U1.G$1_-V
  N5: R2.wiper, R3.Pin_0, U1.G$1_+IN
  N6: LED1.cathode, R5.Pin_0
