# Fritzing sketch NonInvertingAmplifier (saved by Fritzing 0.9.2b)
breadboards: 1

parts:
  5V = Power plug
  IC1 = LM324 [package=dil16]
  IC2 = LM741 [part_number=UA741CN package=dip08]
  IC3 = LM741 [part_number=ML741 package=dip08]
  RL1 = Resistor [tolerance=±5% resistance=1k package=THT]
  RL2 = Resistor [tolerance=±5% resistance=1k package=THT]
  RF1 = Resistor [tolerance=±5% resistance=20k package=THT]
  RF2 = Resistor [tolerance=±5% resistance=20k package=THT]
  RS1 = Resistor [tolerance=±5% resistance=10k package=THT]
  RS2 = Resistor [tolerance=±5% resistance=10k package=THT]
  Rd1 = Resistor [tolerance=±5% resistance=100k package=THT]
  Rd2 = Resistor [tolerance=±5% resistance=100k package=THT]
  C1 = Ceramic Capacitor [capacitance=100nF package="100 mil [THT, multilayer]"]

nets:
  GND: 5V.GND, IC1.GND, IC2.V-, IC3.V-, RL1.Pin_1, RL2.Pin_1, Rd2.Pin_1, C1.0
  VCC: 5V.VCC, IC1.V+, IC2.V+, IC3.V+, Rd1.Pin_0
  N1: IC1.OUT1, IC1.IN1-, IC2.+INPUT
  CH1/FG: IC1.IN1+, IC1.IN2+
  N2: IC1.IN2-, IC1.OUT2, IC3.+INPUT
  VCC/2: IC1.OUT3, IC1.IN3-, RS1.Pin_0, RS2.Pin_0
  N3: IC1.IN3+, Rd1.Pin_1, Rd2.Pin_0, C1.1
  N4: IC2.+OFFSET, IC2.NC
  N5: IC2.-INPUT, RF1.Pin_0, RS1.Pin_1
  CH2: IC2.OUTPUT, RL1.Pin_0, RF1.Pin_1
  N6: IC3.+OFFSET, IC3.NC
  N7: IC3.-INPUT, RF2.Pin_0, RS2.Pin_1
  CH3: IC3.OUTPUT, RL2.Pin_0, RF2.Pin_1

notes:
  ML741

custom parts:
  LM324: LM324 Quad OpAmp
  LM741: General Purpose Operational Amplifier
