# Fritzing sketch Zener (saved by Fritzing 0.9.0b)
breadboards: 1

parts:
  9V = BC9VPC [package=bc9vpc]
  LED1 = LED - 5mm [color="Red (633nm)" package="5 mm [THT]"]
  R2 = Resistor [tolerance=±5% resistance=4.7k package=THT]
  Part1 = Arduino Uno (Rev3)
  Rd1 = Resistor [tolerance=±5% resistance=4.7k package=THT]
  Rd2 = Resistor [tolerance=±5% resistance=4.7k package=THT]
  D1 = Zener Diode [part_number=1N4733 breakdown_voltage=5.1V package="300 mil [THT]"]
  R1 = Resistor [tolerance=±5% resistance=220 package=THT]

nets:
  N1: 9V.V+, R1.Pin_0
  N2: 9V.V-, R2.Pin_0, Part1.GND, Rd2.Pin_0, D1.anode
  N3: LED1.cathode, R2.Pin_1
  N4: LED1.anode, Rd1.Pin_1, D1.cathode, R1.Pin_1
  N5: Part1.A0, Rd1.Pin_0, Rd2.Pin_1
