# Fritzing sketch HamClock (saved by Fritzing 1.0.1rc)
breadboards: 1

parts:
  Raspberry_Pi1 = Raspberry Pi B+
  LED1 = LED - 3mm [color="Red (633nm)" current=0.030A package="3 mm [THT]"]
  R1 = Resistor [tolerance=±5% power=0.25W resistance=1k package=THT]
  R2 = Resistor [tolerance=±5% power=0.25W resistance=10k package=THT]

nets:
  SA_1: Raspberry_Pi1.GPIO20, R1.Pin_1, R2.Pin_1
  GND: Raspberry_Pi1.GND, LED1.cathode, R2.Pin_0
  N1: LED1.anode, R1.Pin_0

notes:
  Satellite Up
