# Fritzing sketch TinyBlink (saved by Fritzing 0.9.0b)
breadboards: 1

parts:
  U2 = attiny85 [package=dip]
  LED1 = LED - 3mm [color="Green (555nm)" package="3 mm [THT]"]
  LED2 = LED - 3mm [color="Blue (430nm)" package="3 mm [THT]"]
  R1 = Resistor [tolerance=±5% resistance=1k package=THT]
  Power_plug1 = Power plug

nets:
  N1: U2.Pin_4, R1.Pin_0, Power_plug1.GND
  N2: U2.Pin_5, LED2.anode
  N3: U2.Pin_6, LED1.anode
  N4: U2.Pin_8, Power_plug1.VCC
  N5: LED1.cathode, LED2.cathode, R1.Pin_1
