# Fritzing sketch TotalSleep (saved by Fritzing 0.9.2b)
breadboards: 1

parts:
  Part1 = Arduino Uno (Rev3)
  U2 = attiny85 [package=dip]
  R1 = Resistor [tolerance=±5% resistance=1k package=THT]
  RESET = Pushbutton [package="[THT]"]
  R3 = Resistor [tolerance=±5% resistance=4.7k package=THT]
  Q1 = Basic FET P-Channel [part_number=BS250 package="DPak [SMD]"]
  R4 = Resistor [tolerance=±5% resistance=1M package=THT]
  C1 = Ceramic Capacitor [capacitance=100nF package="100 mil [THT, multilayer]"]
  Q2 = NPN-Transistor [part_number=BC547 package="TO92 [THT]"]
  LED1 = LED - 3mm [color="Green (555nm)" package="3 mm [THT]"]

nets:
  SS: Part1.D10_PWM/SS, U2.Pin_1
  MOSI: Part1.D11_PWM/MOSI, U2.Pin_5, R3.Pin_0
  MISO: Part1.D12/MISO, U2.Pin_6
  SCK: Part1.D13/SCK, U2.Pin_7
  GND: Part1.GND, U2.Pin_4, R1.Pin_0, RESET.Pin_1, RESET.Pin_2, C1.0, Q2.E
  5V: Part1.5V, Q1.source, R4.Pin_0
  N1: U2.Pin_3, LED1.anode
  vdd: U2.Pin_8, Q1.drain
  N2: R1.Pin_1, LED1.cathode
  N3: RESET.Pin_3, RESET.Pin_4, Q1.Gate, R4.Pin_1, C1.1, Q2.C
  N4: R3.Pin_1, Q2.B

notes:
  Arduino Uno as ISP
  To program the ATtiny, probably need to power the chip directly from 5V to prevent power cut-off during programming.
  After uploading code with the Uno ISP, it should be detached and power of 1.8-5.5V supplied to circuit.
