# Fritzing sketch BetterWithBacon (saved by Fritzing 0.9.0b)
breadboards: 1

parts:
  LCD1 = LCD screen
  Part1 = Arduino Uno (Rev3)
  RE1 = Rotary Encoder [package=THT]

nets:
  VSS: LCD1.VSS, LCD1.R/W, Part1.GND, RE1.EncoderPinA
  VDD: LCD1.VDD, Part1.5V, RE1.EncoderPinB
  N1: LCD1.V0, RE1.EncoderPinC
  N2: LCD1.RS, Part1.D12/MISO
  N3: LCD1.E, Part1.D11_PWM/MOSI
  N4: LCD1.DB4, Part1.D5_PWM
  N5: LCD1.DB5, Part1.D4
  N6: LCD1.DB6, Part1.D3_PWM
  N7: LCD1.DB7, Part1.D2
