# Fritzing sketch JarabeTapatio (saved by Fritzing 0.9.0b)
breadboards: 1

parts:
  J1 = Piezo Speaker
  R1 = Resistor [tolerance=±5% resistance=1k package=THT]
  LED1 = LED - 5mm [color="Red (633nm)" package="5 mm [THT]"]
  Part1 = Arduino Nano (Rev3.0)

nets:
  N1: J1.pin1, LED1.cathode, Part1.GND
  N2: J1.pin2, R1.Pin_0, Part1.D6
  N3: R1.Pin_1, LED1.anode
